// Logisim project computer.circ as structural Verilog
module alu (
  input  [7:0] Data_A,
  input  [7:0] Data_B,
  input  Carry_in,
  input  Invert_A,
  input  Invert_B,
  output [7:0] Result,
  output Carry_out
);

  wire full_adder_2_carry_out, full_adder_3_carry_out, full_adder_4_carry_out, full_adder_5_carry_out,
       full_adder_6_carry_out, full_adder_7_carry_out, full_adder_8_carry_out, multiplexer_1_out,
       multiplexer_2_out, multiplexer_3_out, multiplexer_4_out, multiplexer_5_out, multiplexer_6_out,
       multiplexer_7_out, multiplexer_8_out, not_1_out, not_2_out, not_3_out, not_4_out, not_5_out,
       not_6_out, not_7_out, not_8_out;

  not not_1 (not_1_out, Data_B[7]);
  not not_2 (not_2_out, Data_B[6]);
  not not_3 (not_3_out, Data_B[5]);
  not not_4 (not_4_out, Data_B[4]);
  not not_5 (not_5_out, Data_B[3]);
  not not_6 (not_6_out, Data_B[2]);
  not not_7 (not_7_out, Data_B[1]);
  not not_8 (not_8_out, Data_B[0]);
  Multiplexer multiplexer_1 (.in0(Data_B[7]), .in1(not_1_out), .out(multiplexer_1_out), .sel(Invert_B));
  Multiplexer multiplexer_2 (.in0(Data_B[6]), .in1(not_2_out), .out(multiplexer_2_out), .sel(Invert_B));
  Multiplexer multiplexer_3 (.in0(Data_B[5]), .in1(not_3_out), .out(multiplexer_3_out), .sel(Invert_B));
  Multiplexer multiplexer_4 (.in0(Data_B[4]), .in1(not_4_out), .out(multiplexer_4_out), .sel(Invert_B));
  Multiplexer multiplexer_5 (.in0(Data_B[3]), .in1(not_5_out), .out(multiplexer_5_out), .sel(Invert_B));
  Multiplexer multiplexer_6 (.in0(Data_B[2]), .in1(not_6_out), .out(multiplexer_6_out), .sel(Invert_B));
  Multiplexer multiplexer_7 (.in0(Data_B[1]), .in1(not_7_out), .out(multiplexer_7_out), .sel(Invert_B));
  Multiplexer multiplexer_8 (.in0(Data_B[0]), .in1(not_8_out), .out(multiplexer_8_out), .sel(Invert_B));
  full_adder full_adder_1 (
    .A(Data_A[7]), .B(multiplexer_1_out), .Carry_in(full_adder_2_carry_out), .Result(Result[7]),
    .Carry_out(Carry_out));
  full_adder full_adder_2 (
    .A(Data_A[6]), .B(multiplexer_2_out), .Carry_in(full_adder_3_carry_out), .Result(Result[6]),
    .Carry_out(full_adder_2_carry_out));
  full_adder full_adder_3 (
    .A(Data_A[5]), .B(multiplexer_3_out), .Carry_in(full_adder_4_carry_out), .Result(Result[5]),
    .Carry_out(full_adder_3_carry_out));
  full_adder full_adder_4 (
    .A(Data_A[4]), .B(multiplexer_4_out), .Carry_in(full_adder_5_carry_out), .Result(Result[4]),
    .Carry_out(full_adder_4_carry_out));
  full_adder full_adder_5 (
    .A(Data_A[3]), .B(multiplexer_5_out), .Carry_in(full_adder_6_carry_out), .Result(Result[3]),
    .Carry_out(full_adder_5_carry_out));
  full_adder full_adder_6 (
    .A(Data_A[2]), .B(multiplexer_6_out), .Carry_in(full_adder_7_carry_out), .Result(Result[2]),
    .Carry_out(full_adder_6_carry_out));
  full_adder full_adder_7 (
    .A(Data_A[1]), .B(multiplexer_7_out), .Carry_in(full_adder_8_carry_out), .Result(Result[1]),
    .Carry_out(full_adder_7_carry_out));
  full_adder full_adder_8 (
    .A(Data_A[0]), .B(multiplexer_8_out), .Carry_in(Carry_in), .Result(Result[0]),
    .Carry_out(full_adder_8_carry_out));
endmodule

module full_adder (
  input  A,
  input  B,
  input  Carry_in,
  output Result,
  output Carry_out
);

  wire and_1_out, and_2_out, xor_1_out;

  xor xor_1 (xor_1_out, A, B);
  xor xor_2 (Result, xor_1_out, Carry_in);
  and and_1 (and_1_out, xor_1_out, Carry_in);
  or or_1 (Carry_out, and_1_out, and_2_out);
  and and_2 (and_2_out, A, B);
endmodule
